// Logisim project atm_circuit.circ as structural Verilog: 35 circuits, main circuit main
// deposit_on
module main (
  output [3:0] \확인용output 
);

  wire _0_2_out, _0_out, \_0이_아닌지_확인용_out_2 , _1_2_out, _1_3_out, _1_4_out, _2_2_out, _2_3_out, _3_2_out,
       _3_3_out, _3_4_out, _4_3_out, _4_out, _5_2_out, _5_3_out, _5_out, _6_2_out, _6_out, _7_2_out, _7_out,
       _8_2_out, _8_out, _9_2_out, _9_out, _10_out, _20_out, _30_out, _40_out, _50_out, _70_out, _100_out,
       _120sec, and_1_out, and_2_out, and_3_out, and_4_out, and_5_out, and_6_out, and_7_out, and_8_out,
       and_9_out, and_10_out, and_11_out, and_12_out, and_13_out, and_14_out, and_15_out,
       \changed_n초동안_1출력_버튼입력_1_out_2 , \changed_n초동안_1출력_버튼입력_2_out_2 , clock_1_out, clock_2_out,
       deposit_on_out_3, deposit_out, \deposit_system_1_수행완료 , \deposit_system_1_실패시 , FUNCTION_qn,
       functioning, init, INSERT_ID_qn, INSERT_PIN_q, INSERT_PIN_qn, invalid, invalid2, normal_end,
       not_1_out, not_2_out, not_3_out, not_4_out, not_5_out, not_6_out, not_7_out, one_on, \one_seat_입력됨 ,
       or_1_out, or_2_out, or_3_out, or_4_out, or_6_out, or_7_out, or_8_out, or_10_out, \PIN_System_실패 ,
       plus_normaltransaction, sel_function, SELECT_FUNCTION_qn, switch_out_3, t_ff_1_q, t_ff_2_q, t_ff_3_q,
       ten_on, \ten_seat_입력됨 , withdrawal_on_out_3, withdrawal_out, \withdrawal_system_1_성공 ,
       \withdrawal_system_1_실패 , \단발성_펄스_out_3 , \상승엣지_생성_1_out_3 , \상승엣지_생성_2_out_3 , \상승엣지_생성_3_out_3 ,
       \상승엣지_생성_4_out_3 ;
  wire [2:0] _1, _2, _3, _4, _5;
  wire [3:0] _1_2, _2_2, _3_2, _4_2, _5_2, \_16BIT_TO_BCD_네_번째_수 , \_16BIT_TO_BCD_두번째_수 ,
       \_16BIT_TO_BCD_세번째_수 , \_16BIT_TO_BCD_첫번째수 , bcd_20bit_to_5_bcd_1__1, bcd_20bit_to_5_bcd_1__2,
       bcd_20bit_to_5_bcd_1__3, bcd_20bit_to_5_bcd_1__4, bcd_20bit_to_5_bcd_1__5, check_out_12,
       n0to4bit_1_out_4, \n0입력_처리_1_out_2 , \n0입력_처리_2_out_2 , \n0입력_처리_3_out_2 , \n0입력_처리_4_out_2 ,
       n1to4bit_1_out_4, n2to4bit_1_out_4, n3to4bit_1_out_4, n4to4bit_1_out_4, n5to4bit_1_out_4,
       n6to4bit_1_out_4, n7to4bit_1_out_4, n8to4bit_1_out_4, n9to4bit_1_out_4, one_num, ten_num;
  wire [5:0] \PIN_System__1번_입력 ;
  wire [7:0] bcd_to_7bit_6_out_2, bcd_to_7bit_7_out_2, rom_3_data;
  wire [7:7] bcd_to_7bit_1_out_2, bcd_to_7bit_2_out_2, bcd_to_7bit_3_out_2, bcd_to_7bit_4_out_2,
       bcd_to_7bit_5_out_2;
  wire [15:0] deposit_system_1_output, or_5_out, ram_1_data, register_2_q, register_3_q, rom_1_data,
       \withdrawal_system_1_출력 ;
  wire [19:0] rom_2_data;

  // Transmission_Gate transmission_1: pin names not known
  \changed_n초동안_1출력_버튼입력  \changed_n초동안_1출력_버튼입력_1  (
    .in_1(\PIN_System__1번_입력 [4]), .out_2(\changed_n초동안_1출력_버튼입력_1_out_2 ));
  or or_1 (or_1_out, or_4_out, \PIN_System__1번_입력 [4], \단발성_펄스_out_3 );
  LED u__1 (.in(\PIN_System__1번_입력 [0]));
  LED u__2 (.in(\PIN_System__1번_입력 [1]));
  LED u__3 (.in(\PIN_System__1번_입력 [2]));
  Button u__1_2 (.out(_1_2_out));
  Button u__4 (.out(_4_out));
  Button _7 (.out(_7_out));
  switch_on switch (.\input (INSERT_PIN_q), .clr(or_2_out), .out_3(switch_out_3));
  _60sec_timer _120sec_timer (.\input (switch_out_3), .init(or_2_out), .\output (invalid2));
  or or_2 (or_2_out, init, plus_normaltransaction);
  LED u__4_2 (.in(\PIN_System__1번_입력 [3]));
  LED led_1 (.in(\changed_n초동안_1출력_버튼입력_1_out_2 ));
  Button u__2_2 (.out(_2_2_out));
  Button u__5 (.out(_5_out));
  Button _8 (.out(_8_out));
  Button _0 (.out(_0_out));
  LED led_2 (.in(\PIN_System__1번_입력 [5]));
  J_K_Flip_Flop INSERT_ID (
    .J(functioning), .clk(or_1_out), .K(FUNCTION_qn), .Q(init), .Qn(INSERT_ID_qn), .preset(or_3_out));  // open: en, reset
  Button u__3_2 (.out(_3_2_out));
  Button _6 (.out(_6_out));
  Button _9 (.out(_9_out));
  LED led_3 (.in(init));
  J_K_Flip_Flop INSERT_PIN (
    .J(init), .clk(or_1_out), .K(INSERT_ID_qn), .Q(INSERT_PIN_q), .Qn(INSERT_PIN_qn), .reset(or_3_out));  // open: preset, en
  not not_1 (not_1_out, INSERT_ID_qn);
  \changed_n초동안_1출력_버튼입력  _120SECEnd_display (.in_1(invalid2), .out_2(_120sec));
  LED led_4 (.in(INSERT_PIN_q));
  _1to4bit u_1to4bit_1 (
    .\인에이블 (not_1_out), .\버튼 (_1_2_out), .\클리어 (not_5_out), .out_4(n1to4bit_1_out_4));  // open: out_5
  _2to4bit u_2to4bit_1 (
    .\인에이블 (not_1_out), .\버튼 (_2_2_out), .\클리어 (not_5_out), .out_4(n2to4bit_1_out_4));  // open: out_5
  _3to4bit u_3to4bit_1 (
    .\인에이블 (not_1_out), .\버튼 (_3_2_out), .\클리어 (not_5_out), .out_4(n3to4bit_1_out_4));  // open: out_5
  _4to4bit u_4to4bit_1 (.\인에이블 (not_1_out), .\버튼 (_4_out), .\클리어 (not_5_out), .out_4(n4to4bit_1_out_4));  // open: out_5
  _5to4bit u_5to4bit_1 (.\인에이블 (not_1_out), .\버튼 (_5_out), .\클리어 (not_5_out), .out_4(n5to4bit_1_out_4));  // open: out_5
  _6to4bit u_6to4bit_1 (.\인에이블 (not_1_out), .\버튼 (_6_out), .\클리어 (not_5_out), .out_4(n6to4bit_1_out_4));  // open: out_5
  _7to4bit u_7to4bit_1 (.\인에이블 (not_1_out), .\버튼 (_7_out), .\클리어 (not_5_out), .out_4(n7to4bit_1_out_4));  // open: out_5
  _8to4bit u_8to4bit_1 (.\인에이블 (not_1_out), .\버튼 (_8_out), .\클리어 (not_5_out), .out_4(n8to4bit_1_out_4));  // open: out_5
  _9to4bit u_9to4bit_1 (.\인에이블 (not_1_out), .\버튼 (_9_out), .\클리어 (not_5_out), .out_4(n9to4bit_1_out_4));  // open: out_5
  _0to4bit u_0to4bit_1 (.\인에이블 (not_1_out), .\버튼 (_0_out), .\클리어 (not_5_out), .out_4(n0to4bit_1_out_4));  // open: out_5
  and and_1 (and_1_out, not_5_out, _1_2_out);
  and and_2 (and_2_out, not_5_out, _2_2_out);
  and and_3 (and_3_out, not_5_out, _3_2_out);
  and and_4 (and_4_out, not_5_out, _4_out);
  and and_5 (and_5_out, not_5_out, _5_out);
  and and_6 (and_6_out, not_5_out, _6_out);
  and and_7 (and_7_out, _7_out, not_5_out);
  and and_8 (and_8_out, not_5_out, _8_out);
  and and_9 (and_9_out, not_5_out, _9_out);
  and and_10 (and_10_out, not_5_out, _0_out);
  not not_2 (not_2_out, or_3_out);
  J_K_Flip_Flop SELECT_FUNCTION (
    .J(INSERT_PIN_q), .clk(or_1_out), .K(INSERT_PIN_qn), .Q(sel_function), .Qn(SELECT_FUNCTION_qn),
    .reset(or_3_out));  // open: preset, en
  not not_3 (not_3_out, \_0이_아닌지_확인용_out_2 );
  not not_4 (not_4_out, not_2_out);
  not not_5 (not_5_out, init);
  LED led_5 (.in(sel_function));
  \_4bit_10개중_1택  check (
    .in_1(n1to4bit_1_out_4), .in_2(n2to4bit_1_out_4), .in_3(n3to4bit_1_out_4), .in_4(n4to4bit_1_out_4),
    .in_5(n5to4bit_1_out_4), .in_6(n6to4bit_1_out_4), .in_7(n7to4bit_1_out_4), .in_8(n8to4bit_1_out_4),
    .in_9(n9to4bit_1_out_4), .in_10(n0to4bit_1_out_4), .clear(not_2_out), .out_12(check_out_12));
  Register #(.width(4), .trigger("high")) register_1 (
    .D(check_out_12), .en(not_3_out), .Q(\확인용output ), .clk(not_3_out), .clr(not_4_out));
  J_K_Flip_Flop FUNCTION (
    .J(sel_function), .clk(or_1_out), .K(SELECT_FUNCTION_qn), .Q(functioning), .Qn(FUNCTION_qn),
    .reset(or_3_out));  // open: preset, en
  or or_3 (or_3_out, normal_end, invalid2, invalid, \상승엣지_생성_1_out_3 , \PIN_System_실패 );
  LED led_6 (.in(functioning));
  \_0X16이_아닌지_확인  \_0이_아닌지_확인용  (.in_1(rom_1_data), .out_2(\_0이_아닌지_확인용_out_2 ));
  \상승엣지_생성  \u_단발성_펄스  (.\_1틱 (\_0이_아닌지_확인용_out_2 ), .clear(or_3_out), .out_3(\단발성_펄스_out_3 ));
  ROM #(.addrWidth(4), .dataWidth(16)) rom_1 (.addr(\확인용output ), .data(rom_1_data));  // open: sel
  _7_Segment_Display u_7_segment_display_1 (.b(_120sec), .c(_120sec));  // open: g, f, a, e, d, dp
  \상승엣지_생성  \u_상승엣지_생성_1  (.\_1틱 (1'b1), .out_3(\상승엣지_생성_1_out_3 ));  // open: clear
  \_16비트를_BCD로  _16BIT_TO_BCD (
    .in_1(rom_1_data), .\첫번째수 (\_16BIT_TO_BCD_첫번째수 ), .\두번째_수 (\_16BIT_TO_BCD_두번째_수 ),
    .\세번째_수 (\_16BIT_TO_BCD_세번째_수 ), .\네_번째_수 (\_16BIT_TO_BCD_네_번째_수 ));
  \상승엣지_생성  \u_상승엣지_생성_2  (.\_1틱 (INSERT_PIN_q), .clear(init), .out_3(\상승엣지_생성_2_out_3 ));
  _7_Segment_Display u_7_segment_display_2 (
    .f(_120sec), .a(_120sec), .b(_120sec), .e(_120sec), .d(_120sec), .c(_120sec));  // open: g, dp
  _7_Segment_Display u_7_segment_display_3 (
    .g(_120sec), .a(_120sec), .b(_120sec), .e(_120sec), .d(_120sec));  // open: f, c, dp
  _7_Segment_Display u_7_segment_display_4 (
    .g(_120sec), .f(_120sec), .a(_120sec), .d(_120sec), .c(_120sec));  // open: b, e, dp
  _7_Segment_Display u_7_segment_display_5 (
    .g(_120sec), .f(_120sec), .a(_120sec), .e(_120sec), .d(_120sec));  // open: b, c, dp
  \_0입력_처리  \u_0입력_처리_1  (.in_1(\_16BIT_TO_BCD_첫번째수 ), .out_2(\n0입력_처리_1_out_2 ));
  \_0입력_처리  \u_0입력_처리_2  (.in_1(\_16BIT_TO_BCD_두번째_수 ), .out_2(\n0입력_처리_2_out_2 ));
  _7_Segment_Display u_7_segment_display_6 (.f(_120sec), .a(_120sec), .e(_120sec), .d(_120sec));  // open: g, b, c, dp
  _7_Segment_Display u_7_segment_display_7 (
    .g(_120sec), .f(_120sec), .a(_120sec), .e(_120sec), .d(_120sec));  // open: b, c, dp
  \_0입력_처리  \u_0입력_처리_3  (.in_1(\_16BIT_TO_BCD_세번째_수 ), .out_2(\n0입력_처리_3_out_2 ));
  \_0입력_처리  \u_0입력_처리_4  (.in_1(\_16BIT_TO_BCD_네_번째_수 ), .out_2(\n0입력_처리_4_out_2 ));
  _7_Segment_Display u_7_segment_display_8 (
    .g(_120sec), .b(_120sec), .e(_120sec), .d(_120sec), .c(_120sec));  // open: f, a, dp
  _7_Segment_Display u_7_segment_display_9 (.g(_120sec), .e(_120sec), .c(_120sec));  // open: f, a, b, d, dp
  enhanced_door_lock PIN_System (
    .\첫째 (\n0입력_처리_4_out_2 ), .\둘 (\n0입력_처리_3_out_2 ), .\셋 (\n0입력_처리_2_out_2 ), .\넷 (\n0입력_처리_1_out_2 ),
    .enable(INSERT_PIN_q), ._1(and_1_out), ._2(and_2_out), ._3(and_3_out), ._4(and_4_out), ._5(and_5_out),
    ._6(and_6_out), ._7(and_7_out), ._8(and_8_out), ._9(and_9_out), ._0(and_10_out),
    .\외부초기화 (\상승엣지_생성_2_out_3 ), .\_1번_입력 (\PIN_System__1번_입력 [0]), .\_2번_입력 (\PIN_System__1번_입력 [1]),
    .\_3번_입력 (\PIN_System__1번_입력 [2]), .\_4번_입력 (\PIN_System__1번_입력 [3]), .\성공 (\PIN_System__1번_입력 [4]),
    .\실패 (\PIN_System_실패 ));
  \n초동안_1출력_버튼입력  \_3초_유지  (.in_1(\PIN_System_실패 ), .out_2(\PIN_System__1번_입력 [5]));
  not not_6 (not_6_out, or_8_out);
  RAM #(.addrWidth(4), .dataWidth(16)) ram_1 (
    .addr(\확인용output ), .data(ram_1_data), .clk(clock_1_out), .ld(not_6_out));  // open: sel, clr
  Clock clock_1 (.out(clock_1_out));
  and and_11 (and_11_out, sel_function, withdrawal_out);
  and and_12 (and_12_out, deposit_out, sel_function);
  switch_on switch_on_1 (.\input (or_8_out), .clr(init), .out_3(plus_normaltransaction));
  ROM #(.addrWidth(16), .dataWidth(20)) rom_2 (.addr(ram_1_data), .data(rom_2_data));  // open: sel
  assign ram_1_data = or_8_out ? or_5_out : 16'bz;  // Controlled_Buffer controlled_buffer_1
  or or_4 (or_4_out, and_11_out, and_12_out);
  Synchronous_Counter_16bit synchronous_counter_16bit_1 (
    .enable(plus_normaltransaction), .clear(init), .out_3(normal_end));
  // Probe on ram_1_data
  Register #(.width(16)) register_2 (.D(ram_1_data), .Q(register_2_q), .clk(and_11_out), .clr(or_6_out));  // open: en
  Register #(.width(16)) register_3 (.D(ram_1_data), .Q(register_3_q), .clk(and_12_out), .clr(or_7_out));  // open: en
  assign or_5_out = deposit_system_1_output | \withdrawal_system_1_출력 ;  // OR_Gate or_5, 16 bits wide
  switch_on withdrawal_on (.\input (and_11_out), .clr(\상승엣지_생성_3_out_3 ), .out_3(withdrawal_on_out_3));
  or or_6 (or_6_out, and_14_out, \상승엣지_생성_3_out_3 );
  and and_13 (and_13_out, withdrawal_on_out_3, functioning);
  \상승엣지_생성  \u_상승엣지_생성_3  (.\_1틱 (init), .out_3(\상승엣지_생성_3_out_3 ));  // open: clear
  Button _1_3 (.out(_1_3_out));
  Button _3_3 (.out(_3_3_out));
  Button u__5_2 (.out(_5_2_out));
  Button _10 (.out(_10_out));
  Button _20 (.out(_20_out));
  or or_7 (or_7_out, and_13_out, \상승엣지_생성_3_out_3 );
  withdrawal_system withdrawal_system_1 (
    .\계좌의_잔액 (register_2_q), .\_1만원 (_1_3_out), .\_3만원 (_3_3_out), .\_5만원 (_5_2_out), .\_10만원 (_10_out),
    .\_20만원 (_20_out), .\_30만원 (_30_out), .\_50만원 (_50_out), .\_70만원 (_70_out), .\_100만원 (_100_out),
    .\_40만원 (_40_out), .\초기화 (\상승엣지_생성_3_out_3 ), .enable(and_13_out), .\실패 (\withdrawal_system_1_실패 ),
    .\성공 (\withdrawal_system_1_성공 ), .\출력 (\withdrawal_system_1_출력 ));
  or or_8 (or_8_out, \withdrawal_system_1_성공 , \deposit_system_1_수행완료 );
  BCD_to_7bit bcd_to_7bit_1 (.in_1(bcd_20bit_to_5_bcd_1__3), .out_2({bcd_to_7bit_1_out_2[7], _3_2, _3}));
  Button _30 (.out(_30_out));
  Button _40 (.out(_40_out));
  Button _50 (.out(_50_out));
  Button _70 (.out(_70_out));
  Button _100 (.out(_100_out));
  BCD_to_7bit bcd_to_7bit_2 (.in_1(bcd_20bit_to_5_bcd_1__1), .out_2({bcd_to_7bit_2_out_2[7], _5_2, _5}));
  BCD_20bit_to_5_BCD bcd_20bit_to_5_bcd_1 (
    .in_1(rom_2_data), ._1(bcd_20bit_to_5_bcd_1__1), ._2(bcd_20bit_to_5_bcd_1__2),
    ._3(bcd_20bit_to_5_bcd_1__3), ._4(bcd_20bit_to_5_bcd_1__4), ._5(bcd_20bit_to_5_bcd_1__5));
  BCD_to_7bit bcd_to_7bit_3 (.in_1(bcd_20bit_to_5_bcd_1__2), .out_2({bcd_to_7bit_3_out_2[7], _4_2, _4}));
  \changed_n초동안_1출력_버튼입력  \changed_n초동안_1출력_버튼입력_2  (.in_1(invalid), .out_2(\changed_n초동안_1출력_버튼입력_2_out_2 ));
  or or_9 (invalid, \withdrawal_system_1_실패 , \deposit_system_1_실패시 );
  _7_Segment_Display u_7_segment_display_10 (
    .g(_1_2[3]), .f(_1_2[2]), .a(_1_2[1]), .b(_1_2[0]), .e(_1[2]), .d(_1[1]), .c(_1[0]));  // open: dp
  _7_Segment_Display u_7_segment_display_11 (
    .g(_2_2[3]), .f(_2_2[2]), .a(_2_2[1]), .b(_2_2[0]), .e(_2[2]), .d(_2[1]), .c(_2[0]));  // open: dp
  LED led_7 (.in(sel_function));
  Button withdrawal (.out(withdrawal_out));
  _7_Segment_Display u_7_segment_display_12 (
    .g(_3_2[3]), .f(_3_2[2]), .a(_3_2[1]), .b(_3_2[0]), .e(_3[2]), .d(_3[1]), .c(_3[0]));  // open: dp
  BCD_to_7bit bcd_to_7bit_4 (.in_1(bcd_20bit_to_5_bcd_1__4), .out_2({bcd_to_7bit_4_out_2[7], _2_2, _2}));
  _7_Segment_Display u_7_segment_display_13 (
    .g(\changed_n초동안_1출력_버튼입력_2_out_2 ), .f(\changed_n초동안_1출력_버튼입력_2_out_2 ),
    .b(\changed_n초동안_1출력_버튼입력_2_out_2 ), .e(\changed_n초동안_1출력_버튼입력_2_out_2 ),
    .c(\changed_n초동안_1출력_버튼입력_2_out_2 ));  // open: a, d, dp
  Button deposit (.out(deposit_out));
  _7_Segment_Display u_7_segment_display_14 (
    .g(_5_2[3]), .f(_5_2[2]), .a(_5_2[1]), .b(_5_2[0]), .e(_5[2]), .d(_5[1]), .c(_5[0]));  // open: dp
  _7_Segment_Display u_7_segment_display_15 (
    .g(_4_2[3]), .f(_4_2[2]), .a(_4_2[1]), .b(_4_2[0]), .e(_4[2]), .d(_4[1]), .c(_4[0]));  // open: dp
  BCD_to_7bit bcd_to_7bit_5 (.in_1(bcd_20bit_to_5_bcd_1__5), .out_2({bcd_to_7bit_5_out_2[7], _1_2, _1}));
  switch_on deposit_on (.\input (and_12_out), .clr(\상승엣지_생성_3_out_3 ), .out_3(deposit_on_out_3));
  _7_Segment_Display u_7_segment_display_16 (
    .f(or_10_out), .a(or_10_out), .b(or_10_out), .e(or_10_out), .d(or_10_out), .c(or_10_out));  // open: g, dp
  and and_14 (and_14_out, deposit_on_out_3, functioning);
  Clock clock_2 (.out(clock_2_out));
  not not_7 (not_7_out, t_ff_3_q);
  _7_Segment_Display u_7_segment_display_17 (
    .f(or_10_out), .a(or_10_out), .b(or_10_out), .e(or_10_out), .d(or_10_out), .c(or_10_out));  // open: g, dp
  _7_Segment_Display u_7_segment_display_18 (
    .f(or_10_out), .a(or_10_out), .b(or_10_out), .e(or_10_out), .d(or_10_out), .c(or_10_out));  // open: g, dp
  BCD_to_7bit bcd_to_7bit_6 (.in_1(ten_num), .out_2(bcd_to_7bit_6_out_2));
  Button _1_4 (.out(_1_4_out));
  Button _4_3 (.out(_4_3_out));
  Button _7_2 (.out(_7_2_out));
  and and_15 (and_15_out, not_7_out, \ten_seat_입력됨 );
  _7_Segment_Display u_7_segment_display_19 (
    .f(or_10_out), .a(or_10_out), .b(or_10_out), .e(or_10_out), .d(or_10_out), .c(or_10_out));  // open: g, dp
  LED led_8 (.in(ten_on));
  _7_Segment_Display u_7_segment_display_20 (
    .g(bcd_to_7bit_6_out_2[6]), .f(bcd_to_7bit_6_out_2[5]), .a(bcd_to_7bit_6_out_2[4]),
    .b(bcd_to_7bit_6_out_2[3]), .e(bcd_to_7bit_6_out_2[2]), .d(bcd_to_7bit_6_out_2[1]),
    .c(bcd_to_7bit_6_out_2[0]));  // open: dp
  Button _2_3 (.out(_2_3_out));
  Button _5_3 (.out(_5_3_out));
  Button _8_2 (.out(_8_2_out));
  Button _0_2 (.out(_0_2_out));
  deposit_num_input ten_seat (
    .enable(and_14_out), ._0(_0_2_out), ._1(_1_4_out), ._2(_2_3_out), ._3(_3_4_out), ._4(_4_3_out),
    ._5(_5_3_out), ._6(_6_2_out), ._7(_7_2_out), ._8(_8_2_out), ._9(_9_2_out), .init(\상승엣지_생성_3_out_3 ),
    .\입력됨 (\ten_seat_입력됨 ), .\각_자리 (ten_on), .\해당_자리의_출력 (ten_num));
  LED led_9 (.in(one_on));
  _7_Segment_Display u_7_segment_display_21 (
    .g(bcd_to_7bit_7_out_2[6]), .f(bcd_to_7bit_7_out_2[5]), .a(bcd_to_7bit_7_out_2[4]),
    .b(bcd_to_7bit_7_out_2[3]), .e(bcd_to_7bit_7_out_2[2]), .d(bcd_to_7bit_7_out_2[1]),
    .c(bcd_to_7bit_7_out_2[0]));  // open: dp
  T_Flip_Flop t_ff_1 (
    .clk(clock_2_out), .T(1'b1), .Q(t_ff_1_q), .reset(\상승엣지_생성_3_out_3 ), .en(and_15_out));  // open: Qn, preset
  or or_10 (or_10_out, functioning, sel_function);
  BCD_to_7bit bcd_to_7bit_7 (.in_1(one_num), .out_2(bcd_to_7bit_7_out_2));
  Button _3_4 (.out(_3_4_out));
  Button _6_2 (.out(_6_2_out));
  Button _9_2 (.out(_9_2_out));
  deposit_num_input one_seat (
    .enable(t_ff_3_q), ._0(_0_2_out), ._1(_1_4_out), ._2(_2_3_out), ._3(_3_4_out), ._4(_4_3_out),
    ._5(_5_3_out), ._6(_6_2_out), ._7(_7_2_out), ._8(_8_2_out), ._9(_9_2_out), .init(\상승엣지_생성_3_out_3 ),
    .\입력됨 (\one_seat_입력됨 ), .\각_자리 (one_on), .\해당_자리의_출력 (one_num));
  T_Flip_Flop t_ff_2 (
    .clk(clock_2_out), .T(t_ff_1_q), .Q(t_ff_2_q), .reset(\상승엣지_생성_3_out_3 ), .en(and_15_out));  // open: Qn, preset
  T_Flip_Flop t_ff_3 (
    .clk(clock_2_out), .T(t_ff_2_q), .Q(t_ff_3_q), .reset(\상승엣지_생성_3_out_3 ), .en(and_15_out));  // open: Qn, preset
  \상승엣지_생성  \u_상승엣지_생성_4  (.\_1틱 (\one_seat_입력됨 ), .out_3(\상승엣지_생성_4_out_3 ));  // open: clear
  // Transmission_Gate transmission_2: pin names not known
  ROM rom_3 (.addr({ten_num, one_num}), .data(rom_3_data));  // open: sel
  // Probe on {ten_num, one_num}
  // Probe on rom_3_data
  deposit_system deposit_system_1 (
    .enable(\상승엣지_생성_4_out_3 ), .\input (rom_3_data), .RAM_account(register_3_q),
    .\output (deposit_system_1_output), .\실패시 (\deposit_system_1_실패시 ), .\수행완료 (\deposit_system_1_수행완료 ));

  // Notes on the sheet:
  //   If this LED turns on, enter PIN
  //   success
  //   failure
  //   링카운터
  //   PIN DB
  //   contents of rom_1 (hex, n*v repeats v):
  //   0 1234 5603 4521 3121 6742 2527 1325 8987 6785
  //   4
  //   3
  //   2
  //   1
  //   12초 안에 입력 못하면 끝
  //   account DB
  //   ROM(binary_to_BCD)
  //   contents of rom_2 (hex, n*v repeats v):
  //   0 1 2 3 4 5 6 7 8 9 10 11 12 13 14 15 16 17 18 19 20 21 22 23 24 25 26 27 28 29 30 31 32 33 34 35 36
  //   37 38 39 40 41 42 43 44 45 46 47 48 49 50 51 52 53 54 55 56 57 58 59 60 61 62 63 64 65 66 67 68 69
  //   70 71 72 73 74 75 76 77 78 79 80 81 82 83 84 85 86 87 88 89 90 91 92 93 94 95 96 97 98 99 100 101
  //   102 103 104 105 106 107 108 109 110 111 112 113 114 115 116 117 118 119 120 121 122 123 124 125 126
  //   127 128 129 130 131 132 133 134 135 136 137 138 139 140 141 142 143 144 145 146 147 148 149 150 151
  //   152 153 154 155 156 157 158 159 160 161 162 163 164 165 166 167 168 169 170 171 172 173 174 175 176
  //   177 178 179 180 181 182 183 184 185 186 187 188 189 190 191 192 193 194 195 196 197 198 199 200 201
  //   202 203 204 205 206 207 208 209 210 211 212 213 214 215 216 217 218 219 220 221 222 223 224 225 226
  //   227 228 229 230 231 232 233 234 235 236 237 238 239 240 241 242 243 244 245 246 247 248 249 250 251
  //   252 253 254 255 256 257 258 259 260 261 262 263 264 265 266 267 268 269 270 271 272 273 274 275 276
  //   277 278 279 280 281 282 283 284 285 286 287 288 289 290 291 292 293 294 295 296 297 298 299 300 301
  //   302 303 304 305 306 307 308 309 310 311 312 313 314 315 316 317 318 319 320 321 322 323 324 325 326
  //   327 328 329 330 331 332 333 334 335 336 337 338 339 340 341 342 343 344 345 346 347 348 349 350 351
  //   352 353 354 355 356 357 358 359 360 361 362 363 364 365 366 367 368 369 370 371 372 373 374 375 376
  //   377 378 379 380 381 382 383 384 385 386 387 388 389 390 391 392 393 394 395 396 397 398 399 400 401
  //   402 403 404 405 406 407 408 409 410 411 412 413 414 415 416 417 418 419 420 421 422 423 424 425 426
  //   427 428 429 430 431 432 433 434 435 436 437 438 439 440 441 442 443 444 445 446 447 448 449 450 451
  //   452 453 454 455 456 457 458 459 460 461 462 463 464 465 466 467 468 469 470 471 472 473 474 475 476
  //   477 478 479 480 481 482 483 484 485 486 487 488 489 490 491 492 493 494 495 496 497 498 499 500 501
  //   502 503 504 505 506 507 508 509 510 511 512 513 514 515 516 517 518 519 520 521 522 523 524 525 526
  //   527 528 529 530 531 532 533 534 535 536 537 538 539 540 541 542 543 544 545 546 547 548 549 550 551
  //   552 553 554 555 556 557 558 559 560 561 562 563 564 565 566 567 568 569 570 571 572 573 574 575 576
  //   577 578 579 580 581 582 583 584 585 586 587 588 589 590 591 592 593 594 595 596 597 598 599 600 601
  //   602 603 604 605 606 607 608 609 610 611 612 613 614 615 616 617 618 619 620 621 622 623 624 625 626
  //   627 628 629 630 631 632 633 634 635 636 637 638 639 640 641 642 643 644 645 646 647 648 649 650 651
  //   652 653 654 655 656 657 658 659 660 661 662 663 664 665 666 667 668 669 670 671 672 673 674 675 676
  //   677 678 679 680 681 682 683 684 685 686 687 688 689 690 691 692 693 694 695 696 697 698 699 700 701
  //   702 703 704 705 706 707 708 709 710 711 712 713 714 715 716 717 718 719 720 721 722 723 724 725 726
  //   727 728 729 730 731 732 733 734 735 736 737 738 739 740 741 742 743 744 745 746 747 748 749 750 751
  //   752 753 754 755 756 757 758 759 760 761 762 763 764 765 766 767 768 769 770 771 772 773 774 775 776
  //   777 778 779 780 781 782 783 784 785 786 787 788 789 790 791 792 793 794 795 796 797 798 799 800 801
  //   802 803 804 805 806 807 808 809 810 811 812 813 814 815 816 817 818 819 820 821 822 823 824 825 826
  //   827 828 829 830 831 832 833 834 835 836 837 838 839 840 841 842 843 844 845 846 847 848 849 850 851
  //   852 853 854 855 856 857 858 859 860 861 862 863 864 865 866 867 868 869 870 871 872 873 874 875 876
  //   877 878 879 880 881 882 883 884 885 886 887 888 889 890 891 892 893 894 895 896 897 898 899 900 901
  //   902 903 904 905 906 907 908 909 910 911 912 913 914 915 916 917 918 919 920 921 922 923 924 925 926
  //   927 928 929 930 931 932 933 934 935 936 937 938 939 940 941 942 943 944 945 946 947 948 949 950 951
  //   952 953 954 955 956 957 958 959 960 961 962 963 964 965 966 967 968 969 970 971 972 973 974 975 976
  //   977 978 979 980 981 982 983 984 985 986 987 988 989 990 991 992 993 994 995 996 997 998 999 1000
  //   1001 1002 1003 1004 1005 1006 1007 1008 1009 1010 1011 1012 1013 1014 1015 1016 1017 1018 1019 1020
  //   1021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
  //   screen for withdrawal
  //   if this light on, selcect function
  //   error
  //   screen for deposit
  //   rom for converting BCD to binary
  //   contents of rom_3 (hex, n*v repeats v):
  //   0 1 2 3 4 5 6 7 8 9 6*0 a b c d e f 10 11 12 13 6*0 14 15 16 17 18 19 1a 1b 1c 1d 6*0 1e 1f 20 21 22
  //   23 24 25 26 27 6*0 28 29 2a 2b 2c 2d 2e 2f 30 31 6*0 32 33 34 35 36 37 38 39 3a 3b 6*0 3c 3d 3e 3f
  //   40 41 42 43 44 45 6*0 46 47 48 49 4a 4b 4c 4d 4e 4f 6*0 50 51 52 53 54 55 56 57 58 59 6*0 5a 5b 5c
  //   5d 5e 5f 60 61 62 63
endmodule

module Synchronous_Counter_16bit (
  input  enable,
  input  clear,
  output out_3
);

  wire and_1_out, and_2_out, not_1_out, not_2_out, not_3_out, not_4_out, t_ff_1_q, t_ff_2_q, t_ff_3_q,
       \카운터용_out ;

  Clock \u_카운터용  (.out(\카운터용_out ));
  not not_1 (not_1_out, \카운터용_out );
  not not_2 (not_2_out, \카운터용_out );
  T_Flip_Flop t_ff_1 (.clk(not_1_out), .T(enable), .Q(t_ff_1_q), .reset(clear));  // open: Qn, preset, en
  not not_3 (not_3_out, \카운터용_out );
  T_Flip_Flop t_ff_2 (.clk(not_2_out), .T(t_ff_1_q), .Q(t_ff_2_q), .reset(clear));  // open: Qn, preset, en
  not not_4 (not_4_out, \카운터용_out );
  and and_1 (and_1_out, t_ff_1_q, t_ff_2_q);
  T_Flip_Flop t_ff_3 (.clk(not_3_out), .T(and_1_out), .Q(t_ff_3_q), .reset(clear));  // open: Qn, preset, en
  and and_2 (and_2_out, and_1_out, t_ff_3_q);
  T_Flip_Flop t_ff_4 (.clk(not_4_out), .T(and_2_out), .Q(out_3), .reset(clear));  // open: Qn, preset, en
endmodule

module door_lock (
  input  [4:0] \한 ,
  input  [4:0] \둘 ,
  input  \PIN인풋 ,
  input  [4:0] \셋 ,
  input  [4:0] \넷 ,
  input  [4:0] _0,
  input  [4:0] _1,
  input  [4:0] _2,
  input  [4:0] _3,
  input  [4:0] _4,
  input  [4:0] _5,
  input  [4:0] _6,
  input  [4:0] _7,
  input  [4:0] _8,
  input  [4:0] _9,
  output \성공 ,
  output \실패 
);

  wire and_1_out, and_2_out, and_3_out, and_4_out, and_5_out, and_6_out, and_7_out, and_8_out, and_9_out,
       and_10_out, and_11_out, and_12_out, and_13_out, and_14_out, and_15_out, and_16_out, button_1_out,
       d_ff_1_q, d_ff_2_q, d_ff_3_q, not_1_out, not_2_out, not_3_out, not_4_out, not_5_out, not_6_out,
       not_7_out, not_8_out, not_9_out, not_10_out, not_11_out, not_12_out, not_13_out, not_14_out,
       not_15_out, not_16_out, not_17_out, not_18_out, not_19_out, not_20_out, not_21_out, not_22_out,
       not_23_out, not_24_out, or_1_out, or_2_out, or_3_out, undriven, undriven_2, undriven_3, undriven_4,
       undriven_5, undriven_6, undriven_7, undriven_8, undriven_9, undriven_10, undriven_11, undriven_12,
       undriven_13, undriven_14, undriven_15, undriven_16, undriven_17, undriven_18, undriven_19,
       undriven_20, undriven_21, undriven_22, undriven_23, undriven_24, undriven_25, undriven_26,
       undriven_27, undriven_28, \각_0번들_out , \각_1번들_out , \각_2번들_out , \각_3번들_out , \각_4_번들_out , \넷_0_out ,
       \넷_1_out , \넷_2_out , \넷_3_out , \넷_4_out , \두_0_out , \두_1_out , \두_2_out , \두_3_out , \두_4_out ,
       \셋_0_out , \셋_1_out , \셋_2_out , \셋_3_out , \셋_4_out , \첫_0_out , \첫_1_out , \첫_2_out , \첫_3_out ,
       \첫_4_out ;

  _7_Segment_Display u_7_segment_display_1 (
    .e(undriven), .d(undriven_8), .c(undriven_15), .dp(undriven_22));  // open: g, f, a, b
  _7_Segment_Display u_7_segment_display_2 (
    .g(undriven), .f(undriven_8), .a(undriven_15), .b(undriven_22), .e(undriven_2), .d(undriven_9),
    .c(undriven_16), .dp(undriven_23));
  _7_Segment_Display u_7_segment_display_3 (
    .g(undriven_2), .f(undriven_9), .a(undriven_16), .b(undriven_23), .e(undriven_3), .d(undriven_10),
    .c(undriven_17), .dp(undriven_24));
  _7_Segment_Display u_7_segment_display_4 (
    .g(undriven_3), .f(undriven_10), .a(undriven_17), .b(undriven_24), .e(undriven_4), .d(undriven_11),
    .c(undriven_18), .dp(undriven_25));
  _7_Segment_Display u_7_segment_display_5 (
    .g(undriven_4), .f(undriven_11), .a(undriven_18), .b(undriven_25), .e(undriven_5), .d(undriven_12),
    .c(undriven_19), .dp(undriven_26));
  _7_Segment_Display u_7_segment_display_6 (
    .g(undriven_5), .f(undriven_12), .a(undriven_19), .b(undriven_26), .e(undriven_6), .d(undriven_13),
    .c(undriven_20), .dp(undriven_27));
  _7_Segment_Display u_7_segment_display_7 (
    .g(undriven_6), .f(undriven_13), .a(undriven_20), .b(undriven_27), .e(undriven_7), .d(undriven_14),
    .c(undriven_21), .dp(undriven_28));
  _7_Segment_Display u_7_segment_display_8 (
    .g(undriven_7), .f(undriven_14), .a(undriven_21), .b(undriven_28));  // open: e, d, c, dp
  or \u_각_0번들  (\각_0번들_out , _0[0], _2[0], _3[0], _4[0], _5[0], _6[0], _7[0], _8[0], _9[0], _1[0]);
  or \u_각_1번들  (\각_1번들_out , _0[1], _1[1], _2[1], _3[1], _4[1], _5[1], _6[1], _7[1], _8[1], _9[1]);
  or \u_각_2번들  (\각_2번들_out , _0[2], _1[2], _2[2], _4[2], _5[2], _6[2], _7[2], _8[2], _9[2], _3[2]);
  or \u_각_3번들  (\각_3번들_out , _0[3], _1[3], _2[3], _3[3], _4[3], _5[3], _6[3], _7[3], _8[3], _9[3]);
  or \u_각_4_번들  (\각_4_번들_out , _0[4], _1[4], _2[4], _3[4], _4[4], _5[4], _6[4], _7[4], _8[4], _9[4]);
  xor \u_첫_0  (\첫_0_out , \한 [0], \각_0번들_out );
  xor \u_두_0  (\두_0_out , \각_0번들_out , \둘 [0]);
  xor \u_셋_0  (\셋_0_out , \각_0번들_out , \셋 [0]);
  xor \u_넷_0  (\넷_0_out , \넷 [0], \각_0번들_out );
  xor \u_첫_2  (\첫_2_out , \한 [2], \각_2번들_out );
  xor \u_두_2  (\두_2_out , \둘 [2], \각_2번들_out );
  xor \u_셋_2  (\셋_2_out , \셋 [2], \각_2번들_out );
  xor \u_넷_2  (\넷_2_out , \넷 [2], \각_2번들_out );
  not not_1 (not_1_out, \첫_0_out );
  not not_2 (not_2_out, \두_0_out );
  not not_3 (not_3_out, \셋_0_out );
  not not_4 (not_4_out, \넷_0_out );
  not not_5 (not_5_out, \첫_1_out );
  xor \u_첫_1  (\첫_1_out , \한 [1], \각_1번들_out );
  xor \u_두_1  (\두_1_out , \둘 [1], \각_1번들_out );
  not not_6 (not_6_out, \두_1_out );
  xor \u_셋_1  (\셋_1_out , \셋 [1], \각_1번들_out );
  not not_7 (not_7_out, \셋_1_out );
  xor \u_넷_1  (\넷_1_out , \넷 [1], \각_1번들_out );
  not not_8 (not_8_out, \넷_1_out );
  not not_9 (not_9_out, \첫_2_out );
  not not_10 (not_10_out, \두_2_out );
  not not_11 (not_11_out, \셋_2_out );
  not not_12 (not_12_out, \넷_2_out );
  not not_13 (not_13_out, \첫_4_out );
  xor \u_첫_4  (\첫_4_out , \한 [4], \각_4_번들_out );
  not not_14 (not_14_out, \두_4_out );
  xor \u_두_4  (\두_4_out , \각_4_번들_out , \둘 [4]);
  not not_15 (not_15_out, \셋_4_out );
  xor \u_셋_4  (\셋_4_out , \셋 [4], \각_4_번들_out );
  xor \u_넷_4  (\넷_4_out , \각_4_번들_out , \넷 [4]);
  not not_16 (not_16_out, \넷_4_out );
  and and_1 (and_1_out, \PIN인풋 , and_2_out);
  and and_2 (and_2_out, not_1_out, not_5_out, not_9_out, not_17_out, not_13_out);
  not not_17 (not_17_out, \첫_3_out );
  xor \u_첫_3  (\첫_3_out , \한 [3], \각_3번들_out );
  xor \u_두_3  (\두_3_out , \각_3번들_out , \둘 [3]);
  not not_18 (not_18_out, \두_3_out );
  xor \u_셋_3  (\셋_3_out , \셋 [3], \각_3번들_out );
  not not_19 (not_19_out, \셋_3_out );
  not not_20 (not_20_out, \넷_3_out );
  xor \u_넷_3  (\넷_3_out , \각_3번들_out , \넷 [3]);
  or or_1 (or_1_out, and_1_out, d_ff_1_q);
  not not_21 (not_21_out, d_ff_1_q);
  and and_3 (and_3_out, d_ff_1_q, and_4_out);
  and and_4 (and_4_out, not_2_out, not_14_out, not_6_out, not_10_out, not_18_out);
  and and_5 (and_5_out, \PIN인풋 , not_21_out);
  not not_22 (not_22_out, d_ff_2_q);
  and and_6 (and_6_out, not_3_out, not_7_out, not_11_out, not_19_out, not_15_out);
  or or_2 (or_2_out, d_ff_2_q, and_3_out);
  and and_7 (and_7_out, d_ff_1_q, not_22_out);
  and and_8 (and_8_out, d_ff_2_q, and_6_out);
  and and_9 (and_9_out, not_4_out, not_12_out, not_8_out, not_20_out, not_16_out);
  D_Flip_Flop d_ff_1 (.clk(or_1_out), .D(\PIN인풋 ), .Q(d_ff_1_q), .reset(\실패 ));  // open: Qn, preset, en
  and and_10 (and_10_out, and_5_out, \한 [4], not_13_out);
  not not_23 (not_23_out, d_ff_3_q);
  or or_3 (or_3_out, and_8_out, d_ff_3_q);
  not not_24 (not_24_out, \성공 );
  D_Flip_Flop d_ff_2 (.clk(or_2_out), .D(d_ff_1_q), .Q(d_ff_2_q), .reset(\실패 ));  // open: Qn, preset, en
  and and_11 (and_11_out, and_7_out, \둘 [4], not_14_out);
  and and_12 (and_12_out, or_3_out, not_23_out);
  and and_13 (and_13_out, and_12_out, \셋 [4], not_15_out);
  and and_14 (and_14_out, d_ff_3_q, and_9_out);
  D_Flip_Flop d_ff_3 (.clk(or_3_out), .D(d_ff_2_q), .Q(d_ff_3_q), .reset(\실패 ));  // open: Qn, preset, en
  and and_15 (and_15_out, d_ff_3_q, not_24_out);
  D_Flip_Flop d_ff_4 (.clk(and_14_out), .D(d_ff_3_q), .Q(\성공 ), .reset(\실패 ));  // open: Qn, preset, en
  and and_16 (and_16_out, and_15_out, \넷 [4], not_16_out);
  Button button_1 (.out(button_1_out));
  or or_4 (\실패 , and_10_out, and_11_out, and_13_out, and_16_out, button_1_out);
endmodule

// 1
module _1to4bit (
  input  \인에이블 ,
  input  \버튼 ,
  input  \클리어 ,
  output [3:0] out_4,
  output [4:0] out_5
);

  Register #(.width(4)) register_1 (.D(4'b0001), .en(\인에이블 ), .Q(out_4), .clk(\버튼 ), .clr(\클리어 ));

  assign out_5 = {\버튼 , out_4};
endmodule

// 2
module _2to4bit (
  input  \인에이블 ,
  input  \버튼 ,
  input  \클리어 ,
  output [3:0] out_4,
  output [4:0] out_5
);

  Register #(.width(4)) register_1 (.D(4'b0010), .en(\인에이블 ), .Q(out_4), .clk(\버튼 ), .clr(\클리어 ));

  assign out_5 = {\버튼 , out_4};
endmodule

// 3
module _3to4bit (
  input  \인에이블 ,
  input  \버튼 ,
  input  \클리어 ,
  output [3:0] out_4,
  output [4:0] out_5
);

  Register #(.width(4)) register_1 (.D(4'b0011), .en(\인에이블 ), .Q(out_4), .clk(\버튼 ), .clr(\클리어 ));

  assign out_5 = {\버튼 , out_4};
endmodule

// 4
module _4to4bit (
  input  \인에이블 ,
  input  \버튼 ,
  input  \클리어 ,
  output [3:0] out_4,
  output [4:0] out_5
);

  Register #(.width(4)) register_1 (.D(4'b0100), .en(\인에이블 ), .Q(out_4), .clk(\버튼 ), .clr(\클리어 ));

  assign out_5 = {\버튼 , out_4};
endmodule

// 5
module _5to4bit (
  input  \인에이블 ,
  input  \버튼 ,
  input  \클리어 ,
  output [3:0] out_4,
  output [4:0] out_5
);

  Register #(.width(4)) register_1 (.D(4'b0101), .en(\인에이블 ), .Q(out_4), .clk(\버튼 ), .clr(\클리어 ));

  assign out_5 = {\버튼 , out_4};
endmodule

// 6
module _6to4bit (
  input  \인에이블 ,
  input  \버튼 ,
  input  \클리어 ,
  output [3:0] out_4,
  output [4:0] out_5
);

  Register #(.width(4)) register_1 (.D(4'b0110), .en(\인에이블 ), .Q(out_4), .clk(\버튼 ), .clr(\클리어 ));

  assign out_5 = {\버튼 , out_4};
endmodule

// 7
module _7to4bit (
  input  \인에이블 ,
  input  \버튼 ,
  input  \클리어 ,
  output [3:0] out_4,
  output [4:0] out_5
);

  Register #(.width(4)) register_1 (.D(4'b0111), .en(\인에이블 ), .Q(out_4), .clk(\버튼 ), .clr(\클리어 ));

  assign out_5 = {\버튼 , out_4};
endmodule

// 9
module _9to4bit (
  input  \인에이블 ,
  input  \버튼 ,
  input  \클리어 ,
  output [3:0] out_4,
  output [4:0] out_5
);

  Register #(.width(4)) register_1 (.D(4'b1001), .en(\인에이블 ), .Q(out_4), .clk(\버튼 ), .clr(\클리어 ));

  assign out_5 = {\버튼 , out_4};
endmodule

// 0
module _0to4bit (
  input  \인에이블 ,
  input  \버튼 ,
  input  \클리어 ,
  output [3:0] out_4,
  output [4:0] out_5
);

  Register #(.width(4)) register_1 (.D(4'b0000), .en(\인에이블 ), .Q(out_4), .clk(\버튼 ), .clr(\클리어 ));

  assign out_5 = {\버튼 , out_4};
endmodule

// 8
module _8to4bit (
  input  \인에이블 ,
  input  \버튼 ,
  input  \클리어 ,
  output [3:0] out_4,
  output [4:0] out_5
);

  Register #(.width(4)) register_1 (.D(4'b1000), .en(\인에이블 ), .Q(out_4), .clk(\버튼 ), .clr(\클리어 ));

  assign out_5 = {\버튼 , out_4};
endmodule

module \_16bit_10개중_1택  (
  input  [15:0] in_1,
  input  [15:0] in_2,
  input  [15:0] in_3,
  input  [15:0] in_4,
  input  [15:0] in_5,
  input  [15:0] in_6,
  input  [15:0] in_7,
  input  [15:0] in_8,
  input  [15:0] in_9,
  input  [15:0] in_10,
  output [15:0] out_11
);

  or _1 (out_11[1], in_2[1], in_1[1], in_6[1], in_7[1], in_3[1], in_4[1], in_5[1], in_2[3], in_9[1], in_10[1]);
  or _0 (out_11[0], in_1[0], in_2[0], in_3[0], in_4[0], in_5[0], in_10[0], in_9[0], in_8[0], in_7[0], in_6[0]);
  or _2 (out_11[2], in_1[2], in_6[2], in_8[2], in_7[2], in_9[2], in_10[2], in_2[2], in_3[2], in_4[2], in_5[2]);
  or _3 (out_11[3], in_1[3], in_6[3], in_2[3], in_3[3], in_4[3], in_5[3], in_10[3], in_9[3], in_8[3], in_7[3]);

  assign in_8[1] = in_2[3];
  assign out_11[15:4] = {12{1'b0}};
endmodule

module \다시0_9를_16비트로  (
  input  [3:0] in_1,
  input  [3:0] in_2,
  input  [3:0] in_3,
  input  [3:0] in_4,
  input  [3:0] in_5,
  input  [3:0] in_6,
  input  [3:0] in_7,
  input  [3:0] in_8,
  input  [3:0] in_9,
  input  [3:0] in_10,
  output [15:0] out_11
);

  or _0 (out_11[0], in_1[0], in_2[0], in_3[0], in_4[0], in_5[0], in_7[0], in_8[0], in_9[0], in_10[0], in_6[0]);
  or _1 (out_11[1], in_1[1], in_2[1], in_3[1], in_4[1], in_5[1], in_6[1], in_7[1], in_8[1], in_9[1], in_10[1]);
  or _2 (out_11[2], in_1[2], in_2[2], in_3[2], in_5[2], in_6[2], in_7[2], in_8[2], in_9[2], in_10[2], in_4[2]);
  or _3 (out_11[3], in_1[3], in_2[3], in_3[3], in_4[3], in_5[3], in_6[3], in_8[3], in_7[3], in_10[3], in_9[3]);

  assign out_11[15:4] = {12{1'b0}};
endmodule

module not_0X16 (
  input  [15:0] in_1,
  output out_2
);

  wire and_1_out, and_2_out, and_4_out, and_5_out, not_1_out, not_2_out, not_3_out, not_4_out;

  and and_1 (and_1_out, not_1_out, 1'b1);
  and and_2 (and_2_out, 1'b1, not_2_out);
  not not_1 (not_1_out, in_1[1]);
  not not_2 (not_2_out, in_1[0]);
  and and_3 (out_2, and_2_out, and_1_out, and_4_out, and_5_out);
  and and_4 (and_4_out, not_3_out, 1'b1);
  not not_3 (not_3_out, in_1[2]);
  and and_5 (and_5_out, 1'b1, not_4_out);
  not not_4 (not_4_out, in_1[3]);

  assign in_1[14:4] = {11{in_1[15]}};
endmodule

module \_4bit_10개중_1택  (
  input  [3:0] in_1,
  input  [3:0] in_2,
  input  [3:0] in_3,
  input  [3:0] in_4,
  input  [3:0] in_5,
  input  [3:0] in_6,
  input  [3:0] in_7,
  input  [3:0] in_8,
  input  [3:0] in_9,
  input  [3:0] in_10,
  input  clear,
  output [3:0] out_12
);

  wire _0_out, _1_out, _2_out, _3_out;

  or _0 (_0_out, in_1[0], in_2[0], in_3[0], in_4[0], in_5[0], in_6[0], in_7[0], in_8[0], in_9[0], in_10[0]);
  or _1 (_1_out, in_1[1], in_2[1], in_3[1], in_4[1], in_5[1], in_6[1], in_7[1], in_8[1], in_9[1], in_10[1]);
  or _2 (_2_out, in_1[2], in_2[2], in_3[2], in_4[2], in_5[2], in_6[2], in_7[2], in_8[2], in_9[2], in_10[2]);
  or _3 (_3_out, in_1[3], in_2[3], in_3[3], in_4[3], in_5[3], in_6[3], in_7[3], in_8[3], in_9[3], in_10[3]);
  and and_1 (out_12[0], clear, _0_out);
  and and_2 (out_12[1], _1_out, clear);
  and and_3 (out_12[2], _2_out, clear);
  and and_4 (out_12[3], _3_out, clear);
endmodule

module \_16비트를_BCD로  (
  input  [15:0] in_1,
  output [3:0] \첫번째수 ,
  output [3:0] \두번째_수 ,
  output [3:0] \세번째_수 ,
  output [3:0] \네_번째_수 
);


  assign \네_번째_수  = in_1[15:12];
  assign \두번째_수  = in_1[7:4];
  assign \세번째_수  = in_1[11:8];
  assign \첫번째수  = in_1[3:0];
endmodule

module \_4bit_to_5bit_4번에1  (
  input  [3:0] in_1,
  output [4:0] out_2
);


  assign out_2 = {1'b1, in_1};
endmodule

module \두_5비트가_같은지__다만_4번이_틀렸는지  (
  input  [4:0] \버튼 ,
  input  [4:0] \레지 ,
  output \값이_맞는지 ,
  output \값이_틀렸는지 
);

  wire and_1_out, and_2_out, and_3_out, and_4_out;

  and and_1 (and_1_out, \버튼 [0], \레지 [0]);
  and and_2 (and_2_out, \버튼 [1], \레지 [1]);
  and and_3 (and_3_out, \버튼 [2], \레지 [2]);
  and and_4 (and_4_out, \버튼 [3], \레지 [3]);
  and and_5 (\값이_틀렸는지 , \버튼 [4], \레지 [4]);
  and and_6 (\값이_맞는지 , and_1_out, and_2_out, and_3_out, and_4_out);
endmodule

module \_0X16이_아닌지_확인  (
  input  [15:0] in_1,
  output out_2
);

  wire and_1_out, not_1_out, not_2_out, not_3_out, not_4_out, xor_1_out, xor_2_out, xor_3_out, xor_4_out;

  xor xor_1 (xor_1_out, 1'b0, in_1[12]);
  xor xor_2 (xor_2_out, 1'b0, in_1[13]);
  xor xor_3 (xor_3_out, 1'b0, in_1[14]);
  xor xor_4 (xor_4_out, 1'b0, in_1[15]);
  not not_1 (not_1_out, xor_1_out);
  not not_2 (not_2_out, xor_2_out);
  not not_3 (not_3_out, xor_3_out);
  not not_4 (not_4_out, xor_4_out);
  and and_1 (and_1_out, not_1_out, not_2_out, not_3_out, not_4_out);
  not not_5 (out_2, and_1_out);

  assign in_1[10:0] = {11{in_1[11]}};
  // also tied to GND on the sheet: in_1[11]
endmodule

module \상승엣지_생성  (
  input  \_1틱 ,
  input  clear,
  output out_3
);

  wire clock_1_out, d_ff_1_qn;

  Clock clock_1 (.out(clock_1_out));
  D_Flip_Flop d_ff_1 (.clk(clock_1_out), .D(\_1틱 ), .Qn(d_ff_1_qn), .reset(clear));  // open: Q, preset, en
  and and_1 (out_3, \_1틱 , d_ff_1_qn);
endmodule

module \_1초_대기_입력  (
  input  in_1,
  output out_2
);

  wire and_1_out, and_2_out, clock_1_out, not_1_out, t_ff_1_q, t_ff_2_q;

  Clock clock_1 (.out(clock_1_out));
  and and_1 (and_1_out, out_2, clock_1_out);
  T_Flip_Flop t_ff_1 (.clk(and_1_out), .T(out_2), .Q(t_ff_1_q), .reset(not_1_out));  // open: Qn, preset, en
  S_R_Flip_Flop s_r_ff_1 (.S(in_1), .clk(in_1), .Q(out_2), .preset(in_1), .reset(and_2_out));  // open: R, Qn, en
  not not_1 (not_1_out, out_2);
  T_Flip_Flop t_ff_2 (.clk(and_1_out), .T(t_ff_1_q), .Q(t_ff_2_q), .reset(not_1_out));  // open: Qn, preset, en
  and and_2 (and_2_out, t_ff_2_q, t_ff_1_q);
endmodule

module enhanced_door_lock (
  input  [3:0] \첫째 ,
  input  [3:0] \둘 ,
  input  [3:0] \셋 ,
  input  [3:0] \넷 ,
  input  enable,
  input  _1,
  input  _2,
  input  _3,
  input  _4,
  input  _5,
  input  _6,
  input  _7,
  input  _8,
  input  _9,
  input  _0,
  input  \외부초기화 ,
  output \_1번_입력 ,
  output \_2번_입력 ,
  output \_3번_입력 ,
  output \_4번_입력 ,
  output \성공 ,
  output \실패 
);

  wire _0_out, _1_out, _2_out, _3_out, \_10초를_셉니다_out_3 , button_1_out, button_2_out, button_3_out,
       button_4_out, button_5_out, button_6_out, button_7_out, button_8_out, button_9_out, button_10_out,
       d_ff_1_q, d_ff_2_q, d_ff_3_q, d_ff_4_q, not_1_out, not_2_out, not_3_out, not_4_out, not_5_out,
       not_6_out, not_7_out, not_8_out, not_9_out, not_10_out, not_11_out, not_12_out, not_13_out,
       not_14_out, not_15_out, not_16_out, not_17_out, not_18_out, not_19_out, not_20_out, not_21_out,
       not_22_out, not_23_out, not_24_out, not_25_out, not_26_out, or_1_out, or_2_out, or_3_out, or_4_out,
       or_5_out, or_6_out, or_7_out, or_8_out, or_9_out, or_10_out, or_11_out, or_12_out, or_13_out,
       or_14_out, or_15_out, or_16_out, \네번째수_맞음_out , \넷_0_out , \넷_1_out , \넷_2_out , \넷_4_out , \두_0_out ,
       \두_1_out , \두_2_out , \두_4_out , \두번째수_맞음_out , \상승엣지_생성_1_out_3 , \상승엣지_생성_2_out_3 ,
       \상승엣지_생성_3_out_3 , \상승엣지_생성_4_out_3 , \상승엣지_생성_5_out_3 , \상승엣지_생성_6_out_3 , \상승엣지_생성_7_out_3 ,
       \상승엣지_생성_8_out_3 , \세번째수_맞음_out , \셋_0_out , \셋_1_out , \셋_2_out , \셋_4_out , \첫_0_out , \첫_1_out ,
       \첫_2_out , \첫_4_out , \첫번째수_입력시_out ;
  wire [3:0] register_1_q, register_2_q, register_3_q, register_4_q, register_5_q, register_6_q,
       register_7_q, register_8_q, register_9_q, register_10_q;

  Button button_1 (.out(button_1_out));
  Button button_2 (.out(button_2_out));
  Button button_3 (.out(button_3_out));
  Button button_4 (.out(button_4_out));
  Button button_5 (.out(button_5_out));
  Button button_6 (.out(button_6_out));
  Button button_7 (.out(button_7_out));
  Button button_8 (.out(button_8_out));
  or or_1 (or_1_out, _4, button_9_out);
  Button button_9 (.out(button_9_out));
  or or_2 (or_2_out, _5, button_10_out);
  Button button_10 (.out(button_10_out));
  or or_3 (or_3_out, _6, button_1_out);
  or or_4 (or_4_out, _7, button_2_out);
  or or_5 (or_5_out, _8, button_3_out);
  or or_6 (or_6_out, _9, button_4_out);
  or or_7 (or_7_out, _0, button_5_out);
  or or_8 (or_8_out, _1, button_6_out);
  or or_9 (or_9_out, _2, button_7_out);
  or or_10 (or_10_out, _3, button_8_out);
  or or_11 (or_11_out, or_7_out, or_6_out, or_8_out, or_9_out, or_10_out, or_1_out, or_2_out, or_3_out, or_4_out, or_5_out);
  Register #(.width(4)) register_1 (.D(4'b0001), .en(or_8_out), .Q(register_1_q), .clk(or_8_out), .clr(or_15_out));
  Register #(.width(4)) register_2 (.D(4'b0010), .en(or_9_out), .Q(register_2_q), .clk(or_9_out), .clr(or_15_out));
  Register #(.width(4)) register_3 (.D(4'b0011), .en(or_10_out), .Q(register_3_q), .clk(or_10_out), .clr(or_15_out));
  Register #(.width(4)) register_4 (.D(4'b0100), .en(or_1_out), .Q(register_4_q), .clk(or_1_out), .clr(or_15_out));
  Register #(.width(4)) register_5 (.D(4'b0101), .en(or_2_out), .Q(register_5_q), .clk(or_2_out), .clr(or_15_out));
  Register #(.width(4)) register_6 (.D(4'b0110), .en(or_3_out), .Q(register_6_q), .clk(or_3_out), .clr(or_15_out));
  Register #(.width(4)) register_7 (.D(4'b0111), .en(or_4_out), .Q(register_7_q), .clk(or_4_out), .clr(or_15_out));
  Register #(.width(4)) register_8 (.D(4'b1000), .en(or_5_out), .Q(register_8_q), .clk(or_5_out), .clr(or_15_out));
  Register #(.width(4)) register_9 (.D(4'b1001), .en(or_6_out), .Q(register_9_q), .clk(or_6_out), .clr(or_15_out));
  Register #(.width(4)) register_10 (.D(4'b1111), .en(or_7_out), .Q(register_10_q), .clk(or_7_out), .clr(or_15_out));
  or u__0 (_0_out, register_1_q[0], register_2_q[0], register_3_q[0], register_4_q[0], register_5_q[0], register_10_q[0], register_9_q[0], register_8_q[0], register_7_q[0], register_6_q[0]);
  or u__1 (_1_out, register_1_q[1], register_2_q[1], register_3_q[1], register_4_q[1], register_5_q[1], register_6_q[1], register_7_q[1], register_8_q[1], register_9_q[1], register_10_q[1]);
  or u__2 (_2_out, register_1_q[2], register_2_q[2], register_3_q[2], register_4_q[2], register_5_q[2], register_6_q[2], register_7_q[2], register_10_q[2], register_8_q[2], register_9_q[2]);
  or u__3 (_3_out, register_1_q[3], register_2_q[3], register_3_q[3], register_4_q[3], register_5_q[3], register_6_q[3], register_7_q[3], register_8_q[3], register_9_q[3], register_10_q[3]);
  xor \u_첫_2  (\첫_2_out , \첫째 [2], _2_out);
  xor \u_두_2  (\두_2_out , \둘 [2], _2_out);
  xor \u_셋_2  (\셋_2_out , \셋 [2], _2_out);
  xor \u_넷_2  (\넷_2_out , \넷 [2], _2_out);
  xor \u_첫_4  (\첫_4_out , \첫째 [3], _3_out);
  xor \u_두_4  (\두_4_out , \둘 [3], _3_out);
  xor \u_셋_4  (\셋_4_out , \셋 [3], _3_out);
  xor \u_넷_4  (\넷_4_out , \넷 [3], _3_out);
  not not_1 (not_1_out, \첫_0_out );
  xor \u_첫_0  (\첫_0_out , \첫째 [0], _0_out);
  not not_2 (not_2_out, \두_0_out );
  xor \u_두_0  (\두_0_out , \둘 [0], _0_out);
  not not_3 (not_3_out, \셋_0_out );
  xor \u_셋_0  (\셋_0_out , \셋 [0], _0_out);
  xor \u_넷_0  (\넷_0_out , \넷 [0], _0_out);
  not not_4 (not_4_out, \넷_0_out );
  not not_5 (not_5_out, \첫_1_out );
  xor \u_첫_1  (\첫_1_out , \첫째 [1], _1_out);
  not not_6 (not_6_out, \두_1_out );
  xor \u_두_1  (\두_1_out , \둘 [1], _1_out);
  not not_7 (not_7_out, \셋_1_out );
  xor \u_셋_1  (\셋_1_out , \셋 [1], _1_out);
  not not_8 (not_8_out, \넷_1_out );
  xor \u_넷_1  (\넷_1_out , \넷 [1], _1_out);
  not not_9 (not_9_out, \첫_2_out );
  not not_10 (not_10_out, \두_2_out );
  not not_11 (not_11_out, \셋_2_out );
  not not_12 (not_12_out, \넷_2_out );
  not not_13 (not_13_out, \첫_4_out );
  not not_14 (not_14_out, \두_4_out );
  not not_15 (not_15_out, \셋_4_out );
  not not_16 (not_16_out, \넷_4_out );
  and \u_첫번째수_입력시  (\첫번째수_입력시_out , enable, not_1_out, not_5_out, not_9_out, not_13_out, \상승엣지_생성_1_out_3 );
  \상승엣지_생성  \u_상승엣지_생성_1  (.\_1틱 (or_11_out), .clear(or_16_out), .out_3(\상승엣지_생성_1_out_3 ));
  \상승엣지_생성  \u_상승엣지_생성_2  (.\_1틱 (or_11_out), .clear(or_16_out), .out_3(\상승엣지_생성_2_out_3 ));
  \상승엣지_생성  \u_상승엣지_생성_3  (.\_1틱 (or_11_out), .clear(or_16_out), .out_3(\상승엣지_생성_3_out_3 ));
  \상승엣지_생성  \u_상승엣지_생성_4  (.\_1틱 (or_11_out), .clear(or_16_out), .out_3(\상승엣지_생성_4_out_3 ));
  or or_12 (or_12_out, d_ff_1_q, \첫번째수_입력시_out );
  and \u_두번째수_맞음  (\두번째수_맞음_out , not_2_out, d_ff_1_q, not_6_out, not_10_out, not_14_out, \상승엣지_생성_2_out_3 );
  or or_13 (or_13_out, d_ff_2_q, \두번째수_맞음_out );
  and \u_세번째수_맞음  (\세번째수_맞음_out , not_7_out, d_ff_2_q, not_11_out, not_15_out, not_3_out, \상승엣지_생성_3_out_3 );
  and \u_네번째수_맞음  (\네번째수_맞음_out , not_4_out, \상승엣지_생성_4_out_3 , not_16_out, not_8_out, not_12_out, d_ff_3_q);
  and and_1 (\_1번_입력 , enable, not_17_out, not_18_out);
  not not_17 (not_17_out, or_15_out);
  not not_18 (not_18_out, d_ff_1_q);
  D_Flip_Flop d_ff_1 (.clk(or_12_out), .D(enable), .Q(d_ff_1_q), .reset(or_16_out));  // open: Qn, preset, en
  or or_14 (or_14_out, d_ff_3_q, \세번째수_맞음_out );
  \상승엣지_생성  \u_상승엣지_생성_5  (.\_1틱 (d_ff_1_q), .out_3(\상승엣지_생성_5_out_3 ));  // open: clear
  and and_2 (\_2번_입력 , d_ff_1_q, not_19_out, not_20_out);
  not not_19 (not_19_out, or_15_out);
  not not_20 (not_20_out, d_ff_2_q);
  D_Flip_Flop d_ff_2 (.clk(or_13_out), .D(d_ff_1_q), .Q(d_ff_2_q), .reset(or_16_out));  // open: Qn, preset, en
  not not_21 (not_21_out, enable);
  \상승엣지_생성  \u_상승엣지_생성_6  (.\_1틱 (d_ff_2_q), .out_3(\상승엣지_생성_6_out_3 ));  // open: clear
  or or_15 (or_15_out, \상승엣지_생성_5_out_3 , \상승엣지_생성_6_out_3 , or_16_out, \상승엣지_생성_8_out_3 , \상승엣지_생성_7_out_3 );
  Synchronous_Counter_16bit \_10초를_셉니다  (.enable(enable), .clear(not_21_out), .out_3(\_10초를_셉니다_out_3 ));
  and and_3 (\_3번_입력 , d_ff_2_q, not_22_out, not_23_out);
  not not_22 (not_22_out, or_15_out);
  D_Flip_Flop d_ff_3 (.clk(or_14_out), .D(d_ff_2_q), .Q(d_ff_3_q), .reset(or_16_out));  // open: Qn, preset, en
  \상승엣지_생성  \u_상승엣지_생성_7  (.\_1틱 (d_ff_3_q), .out_3(\상승엣지_생성_7_out_3 ));  // open: clear
  not not_23 (not_23_out, d_ff_3_q);
  D_Flip_Flop d_ff_4 (.clk(\네번째수_맞음_out ), .D(d_ff_3_q), .Q(d_ff_4_q), .reset(or_16_out));  // open: Qn, preset, en
  and and_4 (\_4번_입력 , d_ff_3_q, not_24_out, not_25_out);
  not not_24 (not_24_out, or_15_out);
  not not_25 (not_25_out, d_ff_4_q);
  \상승엣지_생성  \u_상승엣지_생성_8  (.\_1틱 (d_ff_4_q), .out_3(\상승엣지_생성_8_out_3 ));  // open: clear
  not not_26 (not_26_out, d_ff_4_q);
  and and_5 (\실패 , not_26_out, \_10초를_셉니다_out_3 );
  and and_6 (\성공 , enable, d_ff_4_q);
  or or_16 (or_16_out, \외부초기화 , \실패 );
endmodule

module \n초동안_1출력_버튼입력  (
  input  in_1,
  output out_2
);

  wire and_1_out, clock_1_out, counter_1_carry, not_1_out;

  Clock clock_1 (.out(clock_1_out));
  and and_1 (and_1_out, out_2, clock_1_out);
  S_R_Flip_Flop s_r_ff_1 (.S(in_1), .clk(in_1), .Q(out_2), .preset(in_1), .reset(counter_1_carry));  // open: R, Qn, en
  Counter #(.width(2), .max('h3)) counter_1 (
    .count(and_1_out), .carry(counter_1_carry), .clk(and_1_out), .clr(not_1_out));  // open: load, D, Q
  not not_1 (not_1_out, out_2);
endmodule

module \_0입력_처리  (
  input  [3:0] in_1,
  output [3:0] out_2
);

  wire and_1_out, not_1_out, not_2_out, not_3_out, not_4_out;

  not not_1 (not_1_out, in_1[0]);
  not not_2 (not_2_out, in_1[1]);
  not not_3 (not_3_out, in_1[2]);
  not not_4 (not_4_out, in_1[3]);
  or or_1 (out_2[0], and_1_out, in_1[0]);
  or or_2 (out_2[1], and_1_out, in_1[1]);
  or or_3 (out_2[2], and_1_out, in_1[2]);
  or or_4 (out_2[3], in_1[3], and_1_out);
  and and_1 (and_1_out, not_1_out, not_2_out, not_3_out, not_4_out);
endmodule

module BCD_20bit_to_5_BCD (
  input  [19:0] in_1,
  output [3:0] _1,
  output [3:0] _2,
  output [3:0] _3,
  output [3:0] _4,
  output [3:0] _5
);


  assign _1 = in_1[3:0];
  assign _2 = in_1[7:4];
  assign _3 = in_1[11:8];
  assign _4 = in_1[15:12];
  assign _5 = in_1[19:16];
endmodule

module BCD_to_7bit (
  input  [3:0] in_1,
  output [7:0] out_2
);

  _7_Segment_Display u_7_segment_display_1 (.g(1'b1), .f(1'b1), .a(1'b1), .d(1'b1), .c(1'b1));  // open: b, e, dp
  ROM #(.addrWidth(4)) rom_1 (.addr(in_1), .data(out_2));  // open: sel

  // Notes on the sheet:
  //   contents of rom_1 (hex, n*v repeats v):
  //   3f 9 5e 5b 69 73 67 19 7f 79
  //   01110011
  //   01256
endmodule

module \changed_n초동안_1출력_버튼입력  (
  input  in_1,
  output out_2
);

  wire and_1_out, and_2_out, clock_1_out, not_1_out, t_ff_1_q, t_ff_2_q;

  Clock clock_1 (.out(clock_1_out));
  and and_1 (and_1_out, out_2, clock_1_out);
  T_Flip_Flop t_ff_1 (.clk(and_1_out), .T(out_2), .Q(t_ff_1_q), .reset(not_1_out));  // open: Qn, preset, en
  S_R_Flip_Flop s_r_ff_1 (.S(in_1), .clk(in_1), .Q(out_2), .preset(in_1), .reset(and_2_out));  // open: R, Qn, en
  not not_1 (not_1_out, out_2);
  T_Flip_Flop t_ff_2 (.clk(and_1_out), .T(t_ff_1_q), .Q(t_ff_2_q), .reset(not_1_out));  // open: Qn, preset, en
  and and_2 (and_2_out, t_ff_2_q, t_ff_1_q);
endmodule

module withdrawal_system (
  input  [15:0] \계좌의_잔액 ,
  input  \_1만원 ,
  input  \_3만원 ,
  input  \_5만원 ,
  input  \_10만원 ,
  input  \_20만원 ,
  input  \_30만원 ,
  input  \_50만원 ,
  input  \_70만원 ,
  input  \_100만원 ,
  input  \_40만원 ,
  input  \초기화 ,
  input  enable,
  output \실패 ,
  output \성공 ,
  output [15:0] \출력 
);

  wire and_1_out, and_2_out, and_3_out, and_4_out, and_5_out, and_6_out, and_7_out, and_8_out, and_9_out,
       and_10_out, and_11_out, and_12_out, \changed_n초동안_1출력_버튼입력_1_out_2 , \changed_n초동안_1출력_버튼입력_2_out_2 ,
       comparator_1_eq, comparator_1_lt, not_1_out, or_1_out, or_2_out, \상승엣지_생성_1_out_3 , \상승엣지_생성_2_out_3 ;
  wire [6:0] _0_out, register_1_q, register_2_q, register_3_q, register_4_q, register_5_q, register_6_q,
       register_7_q, register_8_q, register_9_q, register_10_q;
  wire [15:0] subtractor_1_out;

  and and_1 (and_1_out, \_1만원 , enable);
  and and_2 (and_2_out, \_3만원 , enable);
  and and_3 (and_3_out, \_5만원 , enable);
  and and_4 (and_4_out, \_10만원 , enable);
  and and_5 (and_5_out, \_20만원 , enable);
  and and_6 (and_6_out, \_30만원 , enable);
  and and_7 (and_7_out, \_50만원 , enable);
  and and_8 (and_8_out, \_70만원 , enable);
  and and_9 (and_9_out, \_100만원 , enable);
  and and_10 (and_10_out, \_40만원 , enable);
  or or_1 (or_1_out, and_1_out, and_2_out, and_3_out, and_4_out, and_5_out, and_10_out, and_6_out, and_7_out, and_8_out, and_9_out);
  Register #(.width(7)) register_1 (.D(7'b0101000), .en(and_10_out), .Q(register_1_q), .clk(and_10_out), .clr(\초기화 ));
  Register #(.width(7)) register_2 (.D(7'b0000001), .en(and_1_out), .Q(register_2_q), .clk(and_1_out), .clr(\초기화 ));
  Register #(.width(7)) register_3 (.D(7'b0000011), .en(and_2_out), .Q(register_3_q), .clk(and_2_out), .clr(\초기화 ));
  Register #(.width(7)) register_4 (.D(7'b0000101), .en(and_3_out), .Q(register_4_q), .clk(and_3_out), .clr(\초기화 ));
  Register #(.width(7)) register_5 (.D(7'b0001010), .en(and_4_out), .Q(register_5_q), .clk(and_4_out), .clr(\초기화 ));
  Register #(.width(7)) register_6 (.D(7'b0010100), .en(and_5_out), .Q(register_6_q), .clk(and_5_out), .clr(\초기화 ));
  Register #(.width(7)) register_7 (.D(7'b0011110), .en(and_6_out), .Q(register_7_q), .clk(and_6_out), .clr(\초기화 ));
  Register #(.width(7)) register_8 (.D(7'b0110010), .en(and_7_out), .Q(register_8_q), .clk(and_7_out), .clr(\초기화 ));
  Register #(.width(7)) register_9 (.D(7'b1000110), .en(and_8_out), .Q(register_9_q), .clk(and_8_out), .clr(\초기화 ));
  Register #(.width(7)) register_10 (.D(7'b1100100), .en(and_9_out), .Q(register_10_q), .clk(and_9_out), .clr(\초기화 ));
  or _0 (_0_out[0], register_2_q[0], register_3_q[0], register_4_q[0], register_5_q[0], register_6_q[0], register_7_q[0], register_8_q[0], register_9_q[0], register_10_q[0], register_1_q[0]);
  or _1 (_0_out[1], register_2_q[1], register_3_q[1], register_4_q[1], register_1_q[1], register_10_q[1], register_9_q[1], register_8_q[1], register_7_q[1], register_6_q[1], register_5_q[1]);
  or _2 (_0_out[2], register_2_q[2], register_3_q[2], register_4_q[2], register_5_q[2], register_6_q[2], register_7_q[2], register_8_q[2], register_9_q[2], register_10_q[2], register_1_q[2]);
  or _3 (_0_out[3], register_2_q[3], register_3_q[3], register_4_q[3], register_5_q[3], register_6_q[3], register_7_q[3], register_8_q[3], register_9_q[3], register_10_q[3], register_1_q[3]);
  or _4 (_0_out[4], register_2_q[4], register_3_q[4], register_4_q[4], register_5_q[4], register_6_q[4], register_7_q[4], register_8_q[4], register_9_q[4], register_10_q[4], register_1_q[4]);
  or _5 (_0_out[5], register_2_q[5], register_3_q[5], register_4_q[5], register_5_q[5], register_6_q[5], register_7_q[5], register_8_q[5], register_9_q[5], register_10_q[5], register_1_q[5]);
  or _6 (_0_out[6], register_2_q[6], register_3_q[6], register_4_q[6], register_5_q[6], register_6_q[6], register_7_q[6], register_8_q[6], register_9_q[6], register_10_q[6], register_1_q[6]);
  Comparator #(.width(16), .mode("unsigned")) comparator_1 (
    .a({{9{1'b0}}, _0_out}), .b(\계좌의_잔액 ), .gt(\실패 ), .eq(comparator_1_eq), .lt(comparator_1_lt));
  // Probe on {{9{1'b0}}, _0_out}
  // Probe on \계좌의_잔액 
  \changed_n초동안_1출력_버튼입력  \changed_n초동안_1출력_버튼입력_1  (.in_1(or_1_out), .out_2(\changed_n초동안_1출력_버튼입력_1_out_2 ));
  or or_2 (or_2_out, comparator_1_eq, comparator_1_lt);
  and and_11 (and_11_out, or_2_out, \changed_n초동안_1출력_버튼입력_1_out_2 );
  Subtractor #(.width(16)) subtractor_1 (
    .a(\계좌의_잔액 ), .b({{9{1'b0}}, _0_out}), .out(subtractor_1_out));  // open: bin, bout
  \상승엣지_생성  \u_상승엣지_생성_1  (.\_1틱 (and_11_out), .out_3(\상승엣지_생성_1_out_3 ));  // open: clear
  and and_12 (and_12_out, \changed_n초동안_1출력_버튼입력_2_out_2 , not_1_out);
  not not_1 (not_1_out, \상승엣지_생성_2_out_3 );
  \상승엣지_생성  \u_상승엣지_생성_2  (.\_1틱 (\changed_n초동안_1출력_버튼입력_2_out_2 ), .out_3(\상승엣지_생성_2_out_3 ));  // open: clear
  // Probe on \출력 
  \changed_n초동안_1출력_버튼입력  \changed_n초동안_1출력_버튼입력_2  (.in_1(\상승엣지_생성_1_out_3 ), .out_2(\changed_n초동안_1출력_버튼입력_2_out_2 ));
  Register #(.width(16)) register_11 (.D(subtractor_1_out), .en(and_12_out), .Q(\출력 ), .clk(and_12_out), .clr(\초기화 ));
  \changed_n초동안_1출력_버튼입력  \changed_n초동안_1출력_버튼입력_3  (.in_1(\changed_n초동안_1출력_버튼입력_2_out_2 ), .out_2(\성공 ));
endmodule

module switch_on (
  input  \input ,
  input  clr,
  output out_3
);

  D_Flip_Flop d_ff_1 (.clk(\input ), .D(\input ), .Q(out_3), .reset(clr));  // open: Qn, preset, en
endmodule

module deposit_num_input (
  input  enable,
  input  _0,
  input  _1,
  input  _2,
  input  _3,
  input  _4,
  input  _5,
  input  _6,
  input  _7,
  input  _8,
  input  _9,
  input  init,
  output \입력됨 ,
  output \각_자리 ,
  output [3:0] \해당_자리의_출력 
);

  wire and_1_out, and_2_out, and_3_out, and_4_out, and_5_out, and_6_out, and_7_out, and_8_out, and_9_out,
       and_10_out, and_13_out, clock_1_out, not_1_out, not_2_out, or_1_out, switch_on_1_out_3,
       \상승엣지_생성_1_out_3 ;
  wire [3:0] _0_out, register_1_q, register_2_q, register_3_q, register_4_q, register_5_q, register_6_q,
       register_7_q, register_8_q, register_9_q, register_10_q;

  and and_1 (and_1_out, _9, enable);
  and and_2 (and_2_out, enable, _0);
  and and_3 (and_3_out, _1, enable);
  and and_4 (and_4_out, _2, enable);
  and and_5 (and_5_out, _3, enable);
  and and_6 (and_6_out, _4, enable);
  and and_7 (and_7_out, _5, enable);
  and and_8 (and_8_out, _6, enable);
  and and_9 (and_9_out, _7, enable);
  Register #(.width(4)) register_1 (.D(4'b0000), .en(and_2_out), .Q(register_1_q), .clk(and_2_out), .clr(init));
  Register #(.width(4)) register_2 (.D(4'b0001), .en(and_3_out), .Q(register_2_q), .clk(and_3_out), .clr(init));
  Register #(.width(4)) register_3 (.D(4'b0010), .en(and_4_out), .Q(register_3_q), .clk(and_4_out), .clr(init));
  Register #(.width(4)) register_4 (.D(4'b0011), .en(and_5_out), .Q(register_4_q), .clk(and_5_out), .clr(init));
  Register #(.width(4)) register_5 (.D(4'b0100), .en(and_6_out), .Q(register_5_q), .clk(and_6_out), .clr(init));
  Register #(.width(4)) register_6 (.D(4'b0101), .en(and_7_out), .Q(register_6_q), .clk(and_7_out), .clr(init));
  Register #(.width(4)) register_7 (.D(4'b0110), .en(and_8_out), .Q(register_7_q), .clk(and_8_out), .clr(init));
  Register #(.width(4)) register_8 (.D(4'b0111), .en(and_9_out), .Q(register_8_q), .clk(and_9_out), .clr(init));
  Register #(.width(4)) register_9 (.D(4'b1000), .en(and_10_out), .Q(register_9_q), .clk(and_10_out), .clr(init));
  and and_10 (and_10_out, _8, enable);
  Register #(.width(4)) register_10 (.D(4'b1001), .en(and_1_out), .Q(register_10_q), .clk(and_1_out), .clr(init));
  or or_1 (or_1_out, and_2_out, and_3_out, and_4_out, and_5_out, and_6_out, and_7_out, and_8_out, and_9_out, and_10_out, and_1_out);
  or u__0 (_0_out[0], register_1_q[0], register_2_q[0], register_3_q[0], register_4_q[0], register_5_q[0], register_6_q[0], register_7_q[0], register_8_q[0], register_9_q[0], register_10_q[0]);
  or u__1 (_0_out[1], register_2_q[1], register_3_q[1], register_4_q[1], register_5_q[1], register_6_q[1], register_7_q[1], register_8_q[1], register_9_q[1], register_10_q[1], register_1_q[1]);
  or u__2 (_0_out[2], register_2_q[2], register_3_q[2], register_4_q[2], register_5_q[2], register_6_q[2], register_7_q[2], register_8_q[2], register_9_q[2], register_10_q[2], register_1_q[2]);
  or u__3 (_0_out[3], register_1_q[3], register_2_q[3], register_3_q[3], register_4_q[3], register_5_q[3], register_6_q[3], register_7_q[3], register_8_q[3], register_9_q[3], register_10_q[3]);
  switch_on switch_on_1 (.\input (or_1_out), .clr(init), .out_3(switch_on_1_out_3));
  not not_1 (not_1_out, switch_on_1_out_3);
  \상승엣지_생성  \u_상승엣지_생성_1  (.\_1틱 (switch_on_1_out_3), .out_3(\상승엣지_생성_1_out_3 ));  // open: clear
  Clock clock_1 (.out(clock_1_out));
  and and_11 (\입력됨 , switch_on_1_out_3, not_2_out);
  not not_2 (not_2_out, and_13_out);
  and and_12 (\각_자리 , not_1_out, enable);
  and and_13 (and_13_out, \상승엣지_생성_1_out_3 , clock_1_out);
  Register #(.width(4)) register_11 (.D(_0_out), .en(and_13_out), .Q(\해당_자리의_출력 ), .clk(and_13_out), .clr(init));
endmodule

module deposit_system (
  input  enable,
  input  [7:0] \input ,
  input  [15:0] RAM_account,
  output [15:0] \output ,
  output \실패시 ,
  output \수행완료 
);

  wire adder_1_cout, \changed_n초동안_1출력_버튼입력_1_out_2 , not_1_out, \상승엣지_생성_1_out_3 ;

  Adder #(.width(16)) adder_1 (
    .a({{8{1'b0}}, \input }), .b(RAM_account), .out(\output ), .cout(adder_1_cout));  // open: cin
  and and_1 (\실패시 , adder_1_cout, enable);
  not not_1 (not_1_out, \실패시 );
  \상승엣지_생성  \u_상승엣지_생성_1  (.\_1틱 (enable), .out_3(\상승엣지_생성_1_out_3 ));  // open: clear
  \changed_n초동안_1출력_버튼입력  \changed_n초동안_1출력_버튼입력_1  (.in_1(\상승엣지_생성_1_out_3 ), .out_2(\changed_n초동안_1출력_버튼입력_1_out_2 ));
  and and_2 (\수행완료 , not_1_out, \changed_n초동안_1출력_버튼입력_1_out_2 );
endmodule

module \_2n초_대기  (
  input  in_1,
  output out_2
);

  wire and_1_out, and_2_out, and_3_out, clock_1_out, not_1_out, t_ff_1_q, t_ff_2_q, t_ff_3_q;

  Clock clock_1 (.out(clock_1_out));
  and and_1 (and_1_out, out_2, clock_1_out);
  T_Flip_Flop t_ff_1 (.clk(and_1_out), .T(out_2), .Q(t_ff_1_q), .reset(not_1_out));  // open: Qn, preset, en
  S_R_Flip_Flop s_r_ff_1 (.S(in_1), .clk(in_1), .Q(out_2), .preset(in_1), .reset(and_2_out));  // open: R, Qn, en
  not not_1 (not_1_out, out_2);
  T_Flip_Flop t_ff_2 (.clk(and_1_out), .T(t_ff_1_q), .Q(t_ff_2_q), .reset(not_1_out));  // open: Qn, preset, en
  and and_2 (and_2_out, t_ff_1_q, t_ff_2_q, t_ff_3_q);
  T_Flip_Flop t_ff_3 (.clk(and_1_out), .T(and_3_out), .Q(t_ff_3_q), .reset(not_1_out));  // open: Qn, preset, en
  and and_3 (and_3_out, t_ff_2_q, t_ff_1_q);
endmodule

module _60sec_timer (
  input  \input ,
  input  init,
  output \output 
);

  wire and_2_out, and_3_out, and_4_out, and_5_out, clock_1_out, j_k_ff_1_q, j_k_ff_2_q, j_k_ff_3_q,
       j_k_ff_4_q, j_k_ff_5_q, j_k_ff_6_q;

  Clock clock_1 (.out(clock_1_out));
  J_K_Flip_Flop j_k_ff_1 (
    .J(\input ), .clk(clock_1_out), .K(\input ), .Q(j_k_ff_1_q), .reset(init));  // open: Qn, preset, en
  and and_1 (\output , j_k_ff_3_q, j_k_ff_4_q, j_k_ff_5_q, j_k_ff_6_q);
  and and_2 (and_2_out, j_k_ff_2_q, j_k_ff_1_q);
  J_K_Flip_Flop j_k_ff_2 (
    .J(j_k_ff_1_q), .clk(clock_1_out), .K(j_k_ff_1_q), .Q(j_k_ff_2_q), .reset(init));  // open: Qn, preset, en
  and and_3 (and_3_out, j_k_ff_1_q, j_k_ff_2_q, j_k_ff_3_q);
  J_K_Flip_Flop j_k_ff_3 (
    .J(and_2_out), .clk(clock_1_out), .K(and_2_out), .Q(j_k_ff_3_q), .reset(init));  // open: Qn, preset, en
  and and_4 (and_4_out, j_k_ff_4_q, j_k_ff_3_q, j_k_ff_2_q, j_k_ff_1_q);
  J_K_Flip_Flop j_k_ff_4 (
    .J(and_3_out), .clk(clock_1_out), .K(and_3_out), .Q(j_k_ff_4_q), .reset(init));  // open: Qn, preset, en
  J_K_Flip_Flop j_k_ff_5 (
    .J(and_4_out), .clk(clock_1_out), .K(and_4_out), .Q(j_k_ff_5_q), .reset(init));  // open: Qn, preset, en
  and and_5 (and_5_out, j_k_ff_5_q, j_k_ff_4_q, j_k_ff_3_q, j_k_ff_2_q, j_k_ff_1_q);
  J_K_Flip_Flop j_k_ff_6 (
    .J(and_5_out), .clk(clock_1_out), .K(and_5_out), .Q(j_k_ff_6_q), .reset(init));  // open: Qn, preset, en
endmodule
